// Logisim project lab2circuit.circ as structural Verilog: 9 circuits, main circuit main
module main (
  input  d2,
  input  d1,
  input  d0
);

  wire namelogic_1_out_4, namelogic_1_s1, namelogic_1_s2, namelogic_1_s3, namelogic_1_s4, namelogic_1_s5,
       namelogic_1_s6;

  namelogic namelogic_1 (
    .out_4(namelogic_1_out_4), .S1(namelogic_1_s1), .S2(namelogic_1_s2), .S3(namelogic_1_s3),
    .S4(namelogic_1_s4), .S5(namelogic_1_s5), .S6(namelogic_1_s6), .d1(d1), .d0(d0), .d2(d2));
  _7_Segment_Display u_7_segment_display_1 (
    .g(namelogic_1_s6), .f(namelogic_1_s5), .a(namelogic_1_out_4), .b(namelogic_1_s1), .e(namelogic_1_s4),
    .d(namelogic_1_s3), .c(namelogic_1_s2));  // open: dp
endmodule

module namelogic (
  input  d2,
  input  d1,
  input  d0,
  output out_4,
  output S1,
  output S2,
  output S3,
  output S4,
  output S5,
  output S6
);

  subS0 subs0_1 (.d2(d2), .d1(d1), .d0(d0), .S0(out_4));
  subS2 subs2_1 (.d2(d2), .d1(d1), .d0(d0), .S2(S2));
  subS3 subs3_1 (.d2(d2), .d1(d1), .d0(d0), .S3(S3));
  subS4 subs4_1 (.d2(d2), .d1(d1), .d0(d0), .S4(S4));
  subS5 subs5_1 (.d2(d2), .d1(d1), .d0(d0), .S5(S5));
  subS6 subs6_1 (.d2(d2), .d1(d1), .d0(d0), .S6(S6));
  subS1 subs1_1 (.d2(d2), .d1(d1), .d0(d0), .S1(S1));
endmodule

module subS0 (
  input  d2,
  input  d1,
  input  d0,
  output S0
);

  not not_1 (S0, 1'b1);
  not not_2 (S0, 1'b1);
  not not_3 (S0, 1'b1);
endmodule

module subS1 (
  input  d2,
  input  d1,
  input  d0,
  output S1
);

  wire and_1_out, and_2_out, not_1_out, not_2_out;

  not not_1 (not_1_out, d2);
  not not_2 (not_2_out, d1);
  and and_1 (and_1_out, not_1_out, not_2_out);
  and and_2 (and_2_out, not_1_out, d0);
  or or_1 (S1, and_1_out, and_2_out);
endmodule

module subS2 (
  input  d2,
  input  d1,
  input  d0,
  output S2
);

  wire and_1_out, and_2_out, not_1_out, not_2_out, not_3_out;

  not not_1 (not_1_out, d2);
  not not_2 (not_2_out, d1);
  not not_3 (not_3_out, d0);
  and and_1 (and_1_out, not_2_out, not_3_out);
  and and_2 (and_2_out, not_1_out, d0);
  or or_1 (S2, and_1_out, and_2_out);
endmodule

module subS3 (
  input  d2,
  input  d1,
  input  d0,
  output S3
);

  not not_1 (S3, d2);
endmodule

module subS4 (
  input  d2,
  input  d1,
  input  d0,
  output S4
);

  wire and_1_out, and_2_out, and_3_out, not_1_out, not_2_out, not_3_out;

  not not_1 (not_1_out, d1);
  not not_2 (not_2_out, d0);
  not not_3 (not_3_out, d2);
  and and_1 (and_1_out, d2, not_1_out, not_2_out);
  and and_2 (and_2_out, not_3_out, d0);
  and and_3 (and_3_out, not_3_out, d1);
  or or_1 (S4, and_1_out, and_2_out, and_3_out);
endmodule

module subS5 (
  input  d2,
  input  d1,
  input  d0,
  output S5
);

  not not_1 (S5, d2);
endmodule

module subS6 (
  input  d2,
  input  d1,
  input  d0,
  output S6
);

  wire not_1_out, not_2_out;

  not not_1 (not_1_out, d1);
  not not_2 (not_2_out, d0);
  and and_1 (S6, not_1_out, not_2_out);
endmodule
