// Logisim project lab3a.circ as structural Verilog: 2 circuits, main circuit mux2to1
module mux2to1 (
  input  [3:0] x,
  input  s,
  input  [3:0] y,
  output [3:0] m
);

  wire [3:0] and_1_out, and_2_out, not_1_out;

  assign not_1_out = ~{4{s}};  // NOT_Gate not_1, 4 bits wide
  assign and_1_out = x & not_1_out;  // AND_Gate and_1, 4 bits wide
  assign and_2_out = {4{s}} & y;  // AND_Gate and_2, 4 bits wide
  assign m = and_1_out | and_2_out;  // OR_Gate or_1, 4 bits wide
endmodule

module mux8to1 (
  input  [2:0] S,
  input  [3:0] Input0,
  input  [3:0] Input1,
  input  [3:0] Input2,
  input  [3:0] Input3,
  input  [3:0] Input4,
  input  [3:0] Input5,
  input  [3:0] Input6,
  input  [3:0] Input7,
  output [3:0] M
);

  wire [3:0] mux2to1_1_m, mux2to1_2_m, mux2to1_3_m, mux2to1_4_m, mux2to1_5_m, mux2to1_6_m;

  mux2to1 mux2to1_1 (.x(Input0), .s(S[0]), .y(Input1), .m(mux2to1_1_m));
  mux2to1 mux2to1_2 (.x(Input2), .s(S[0]), .y(Input3), .m(mux2to1_2_m));
  mux2to1 mux2to1_3 (.x(Input4), .s(S[0]), .y(Input5), .m(mux2to1_3_m));
  mux2to1 mux2to1_4 (.x(Input6), .s(S[0]), .y(Input7), .m(mux2to1_4_m));
  mux2to1 mux2to1_5 (.x(mux2to1_1_m), .s(S[1]), .y(mux2to1_2_m), .m(mux2to1_5_m));
  mux2to1 mux2to1_6 (.x(mux2to1_3_m), .s(S[1]), .y(mux2to1_4_m), .m(mux2to1_6_m));
  mux2to1 mux2to1_7 (.x(mux2to1_5_m), .s(S[2]), .y(mux2to1_6_m), .m(M));
endmodule
