// Logisim project lab3b.circ as structural Verilog: 2 circuits, main circuit fa
module fa (
  input  X,
  input  Y,
  input  Cin,
  output Cout,
  output S
);

  wire and_1_out, and_2_out, xor_1_out;

  or or_1 (Cout, and_1_out, and_2_out);
  and and_1 (and_1_out, X, Y);
  and and_2 (and_2_out, xor_1_out, Cin);
  xor xor_1 (xor_1_out, X, Y);
  xor xor_2 (S, xor_1_out, Cin);
endmodule

module adder4 (
  input  [3:0] Y,
  input  Sub,
  input  [3:0] X,
  output C,
  output [3:0] S
);

  wire fa_1_cout, fa_2_cout, fa_3_cout, xor_1_out, xor_2_out, xor_3_out, xor_4_out;

  xor xor_1 (xor_1_out, Sub, Y[0]);
  fa fa_1 (.X(X[0]), .Y(xor_1_out), .Cin(Sub), .Cout(fa_1_cout), .S(S[0]));
  xor xor_2 (xor_2_out, Sub, Y[1]);
  fa fa_2 (.X(X[1]), .Y(xor_2_out), .Cin(fa_1_cout), .Cout(fa_2_cout), .S(S[1]));
  xor xor_3 (xor_3_out, Sub, Y[2]);
  xor xor_4 (xor_4_out, Sub, Y[3]);
  fa fa_3 (.X(X[2]), .Y(xor_3_out), .Cin(fa_2_cout), .Cout(fa_3_cout), .S(S[2]));
  fa fa_4 (.X(X[3]), .Y(xor_4_out), .Cin(fa_3_cout), .Cout(C), .S(S[3]));
endmodule
