// Logisim project lab4circuit.circ as structural Verilog: 4 circuits, main circuit main
module main (
  input  S,
  input  R,
  input  D1,
  input  D2,
  output notQ1,
  output Q1,
  output notQ2,
  output Q2,
  output notQ3,
  output Q3
);

  wire Clock_out;

  Button Clock (.out(Clock_out));
  GatedSRLatch gatedsrlatch_1 (.S(S), .Clk(Clock_out), .R(R), .notQ(notQ1), .Q(Q1));
  GatedDLatch gateddlatch_1 (.D(D1), .C(Clock_out), .notQ(notQ2), .Q(Q2));
  petdff petdff_1 (.D(D2), .Clock(Clock_out), .notQ(notQ3), .Q(Q3));
endmodule

module GatedSRLatch (
  input  S,
  input  Clk,
  input  R,
  output notQ,
  output Q
);

  wire and_1_out, and_2_out;

  and and_1 (and_1_out, S, Clk);
  and and_2 (and_2_out, Clk, R);
  nor nor_1 (notQ, and_1_out, Q);
  nor nor_2 (Q, notQ, and_2_out);
endmodule

module GatedDLatch (
  input  D,
  input  C,
  output notQ,
  output Q
);

  wire not_1_out;

  not not_1 (not_1_out, D);
  GatedSRLatch gatedsrlatch_1 (.S(D), .Clk(C), .R(not_1_out), .notQ(notQ), .Q(Q));
endmodule

module petdff (
  input  D,
  input  Clock,
  output notQ,
  output Q
);

  wire gateddlatch_1_q, not_1_out, not_2_out;

  not not_1 (not_1_out, Clock);
  not not_2 (not_2_out, not_1_out);
  GatedDLatch gateddlatch_1 (.D(D), .C(not_1_out), .Q(gateddlatch_1_q));  // open: notQ
  GatedDLatch gateddlatch_2 (.D(gateddlatch_1_q), .C(not_2_out), .notQ(notQ), .Q(Q));
endmodule
