// Logisim project lab5.circ as structural Verilog: 3 circuits, main circuit main
module main (
);

  wire Clk_out, dipswitch_1_sw1, dipswitch_1_sw2, F1_q, F2_q, outputlogic_1_l, outputlogic_1_r, reset_out,
       statelogic_1_newf1, statelogic_1_newf2;

  DipSwitch #(.number(2)) dipswitch_1 (.sw1(dipswitch_1_sw1), .sw2(dipswitch_1_sw2));
  Button Clk (.out(Clk_out));
  Button reset (.out(reset_out));
  D_Flip_Flop F2 (.D(statelogic_1_newf2), .clk(Clk_out), .Q(F2_q), .reset(reset_out));  // open: Qn, preset
  statelogic statelogic_1 (
    .F2(F2_q), .F1(F1_q), .A(dipswitch_1_sw1), .B(dipswitch_1_sw2), .newF2(statelogic_1_newf2),
    .newF1(statelogic_1_newf1));
  D_Flip_Flop F1 (.D(statelogic_1_newf1), .clk(Clk_out), .Q(F1_q), .reset(reset_out));  // open: Qn, preset
  LED R (.in(outputlogic_1_r));
  outputlogic outputlogic_1 (.F2(F2_q), .F1(F1_q), .R(outputlogic_1_r), .L(outputlogic_1_l));
  LED L (.in(outputlogic_1_l));
endmodule

module statelogic (
  input  F2,
  input  F1,
  input  A,
  input  B,
  output newF2,
  output newF1
);

  wire and_1_out, and_2_out, and_3_out, and_4_out, not_1_out, not_2_out;

  not not_1 (not_1_out, A);
  not not_2 (not_2_out, B);
  and and_1 (and_1_out, F1, not_1_out, not_2_out);
  and and_2 (and_2_out, F2, not_1_out);
  and and_3 (and_3_out, F2, B);
  and and_4 (and_4_out, F2, F1);
  or or_1 (newF1, and_1_out, and_2_out, and_3_out, and_4_out);

  assign newF2 = A;
endmodule

module outputlogic (
  input  F2,
  input  F1,
  output R,
  output L
);

  wire not_1_out, not_2_out;

  not not_1 (not_1_out, F2);
  not not_2 (not_2_out, F1);
  and and_1 (R, F2, not_2_out);
  and and_2 (L, not_1_out, F1);
endmodule
