// Logisim project lab6_base.circ as structural Verilog: 4 circuits, main circuit main
module DataPath (
  input  R1mul,
  input  R1en,
  input  R2mul,
  input  R2en,
  input  CLK,
  input  reset,
  input  [7:0] X,
  input  [7:0] A,
  input  [7:0] B,
  input  [7:0] C,
  input  [1:0] InSel,
  input  [1:0] ASel,
  input  [1:0] BSel,
  output [7:0] Res
);

  wire [7:0] adder_1_out, multiplexer_1_out, multiplexer_2_out, multiplexer_3_out, multiplexer_4_out,
       multiplexer_5_out, multiplier_1_out, R2_q;

  Multiplexer #(.enable("false"), .width(8)) multiplexer_1 (
    .in0(adder_1_out), .in1(multiplier_1_out), .out(multiplexer_1_out), .sel(R1mul));
  Multiplexer #(.enable("false"), .width(8)) multiplexer_2 (
    .in0(adder_1_out), .in1(multiplier_1_out), .out(multiplexer_2_out), .sel(R2mul));
  Register R1 (.D(multiplexer_1_out), .en(R1en), .clk(CLK), .Q(Res), .clr(reset));
  Register R2 (.D(multiplexer_2_out), .en(R2en), .clk(CLK), .Q(R2_q), .clr(reset));
  Multiplexer #(.enable("false"), .select(2), .width(8)) multiplexer_3 (
    .in0(X), .in1(A), .in2(B), .in3(C), .out(multiplexer_3_out), .sel(InSel));
  Multiplexer #(.enable("false"), .select(2), .width(8)) multiplexer_4 (
    .in0({8{1'b0}}), .in1(Res), .in2(R2_q), .in3(multiplexer_3_out), .out(multiplexer_4_out), .sel(BSel));
  Multiplexer #(.enable("false"), .select(2), .width(8)) multiplexer_5 (
    .in0({8{1'b0}}), .in1(Res), .in2(R2_q), .in3(multiplexer_3_out), .out(multiplexer_5_out), .sel(ASel));
  Multiplier multiplier_1 (.a(multiplexer_4_out), .b(multiplexer_5_out), .out(multiplier_1_out));  // open: cin, cout
  Adder adder_1 (.a(multiplexer_4_out), .b(multiplexer_5_out), .out(adder_1_out));  // open: cin, cout

  // Notes on the sheet:
  //   constant zero
endmodule

module main (
  input  [7:0] X,
  input  [7:0] A,
  input  [7:0] B,
  input  [7:0] C
);

  wire CLK_out, controller_1_done, controller_1_r1en, controller_1_r1mul, controller_1_r2en,
       controller_1_r2mul, reset_out;
  wire [1:0] controller_1_asel, controller_1_bsel, controller_1_insel;
  wire [7:0] datapath_1_res;

  Button CLK (.out(CLK_out));
  Button reset (.out(reset_out));
  Controller controller_1 (
    .CLK(CLK_out), .reset(reset_out), .R1mul(controller_1_r1mul), .R1en(controller_1_r1en),
    .R2mul(controller_1_r2mul), .R2en(controller_1_r2en), .InSel(controller_1_insel),
    .ASel(controller_1_asel), .BSel(controller_1_bsel), .Done(controller_1_done));
  DataPath datapath_1 (
    .R1mul(controller_1_r1mul), .R1en(controller_1_r1en), .R2mul(controller_1_r2mul),
    .R2en(controller_1_r2en), .CLK(CLK_out), .reset(reset_out), .X(X), .A(A), .B(B), .C(C),
    .InSel(controller_1_insel), .ASel(controller_1_asel), .BSel(controller_1_bsel), .Res(datapath_1_res));
  LED led_1 (.in(controller_1_done));
  Hex_Digit_Display hex_digit_display_1 (.value(datapath_1_res[7:4]));  // open: dp
  Hex_Digit_Display hex_digit_display_2 (.value(datapath_1_res[3:0]));  // open: dp

  // Notes on the sheet:
  //   Answer ready
endmodule

module Controller (
  input  CLK,
  input  reset,
  output R1mul,
  output R1en,
  output R2mul,
  output R2en,
  output [1:0] InSel,
  output [1:0] ASel,
  output [1:0] BSel,
  output Done
);

  wire [2:0] controllerlogic_1_nextstep, d_ff_2_q;

  D_Flip_Flop d_ff_1 (
    .D(controllerlogic_1_nextstep[1]), .clk(CLK), .Q(d_ff_2_q[1]), .reset(reset));  // open: Qn, preset
  D_Flip_Flop d_ff_2 (
    .D(controllerlogic_1_nextstep[0]), .clk(CLK), .Q(d_ff_2_q[0]), .reset(reset));  // open: Qn, preset
  ControllerLogic controllerlogic_1 (
    .Step(d_ff_2_q), .R1mul(R1mul), .R1en(R1en), .R2mul(R2mul), .R2en(R2en), .InSel(InSel), .ASel(ASel),
    .BSel(BSel), .Done(Done), .NextStep(controllerlogic_1_nextstep));
  D_Flip_Flop d_ff_3 (
    .D(controllerlogic_1_nextstep[2]), .clk(CLK), .Q(d_ff_2_q[2]), .reset(reset));  // open: Qn, preset
endmodule

module ControllerLogic (
  input  [2:0] Step,
  output R1mul,
  output R1en,
  output R2mul,
  output R2en,
  output [1:0] InSel,
  output [1:0] ASel,
  output [1:0] BSel,
  output Done,
  output [2:0] NextStep
);

  wire and_1_out, and_2_out, and_3_out, and_4_out, and_5_out, and_6_out, and_7_out, and_8_out, and_9_out,
       and_10_out, and_12_out, and_13_out, and_14_out, and_15_out, and_16_out, not_2_out, not_3_out;

  not not_1 (R1mul, Step[2]);
  not not_2 (not_2_out, Step[1]);
  not not_3 (not_3_out, Step[0]);
  and and_1 (and_1_out, not_2_out, Step[0]);
  and and_2 (and_2_out, R1mul, Step[1], not_3_out);
  or or_1 (R1en, and_1_out, and_2_out, and_3_out);
  and and_3 (and_3_out, Step[2], not_2_out);
  and and_4 (and_4_out, R1mul, not_2_out, not_3_out);
  or or_2 (R2en, and_4_out, and_5_out);
  and and_5 (and_5_out, Step[1], Step[0]);
  and and_6 (and_6_out, Step[1], not_3_out);
  or or_3 (InSel[0], and_6_out, Step[2]);
  or or_4 (ASel[1], R1mul, Step[0]);
  or or_5 (ASel[0], not_3_out, Step[1], Step[2]);
  and and_7 (and_7_out, R1mul, Step[0]);
  or or_6 (BSel[1], and_7_out, and_8_out);
  and and_8 (and_8_out, Step[2], not_3_out);
  and and_9 (and_9_out, Step[1], not_3_out);
  or or_7 (BSel[0], and_9_out, and_10_out);
  and and_10 (and_10_out, Step[2], Step[0]);
  and and_11 (Done, Step[2], Step[1]);
  and and_12 (and_12_out, Step[1], Step[0]);
  or or_8 (NextStep[2], and_12_out, Step[2]);
  and and_13 (and_13_out, not_2_out, Step[0]);
  or or_9 (NextStep[1], and_13_out, and_14_out);
  and and_14 (and_14_out, Step[1], not_3_out);
  and and_15 (and_15_out, R1mul, not_3_out);
  or or_10 (NextStep[0], and_15_out, and_16_out);
  and and_16 (and_16_out, not_2_out, not_3_out);

  assign InSel[1] = Step[0];
  assign R2mul = Step[1];
endmodule
