// Logisim project lab07_base.circ as structural Verilog: 4 circuits, main circuit register_file
module register_file (
  input  [7:0] data_write,
  input  clear,
  input  write_enable,
  input  [1:0] read_reg,
  input  [1:0] write_reg,
  input  clk,
  input  reset,
  output [7:0] data_read
);

  wire and_1_out, and_2_out, and_3_out, and_4_out, and_5_out, decoder_1_out0, decoder_1_out1, decoder_1_out2,
       decoder_1_out3, not_1_out;
  wire [7:0] multiplexer_1_out, Reg0_q, Reg1_q, Reg2_q, Reg3_q;

  and and_1 (and_1_out, clear, write_enable, not_1_out);
  not not_1 (not_1_out, clk);
  Multiplexer #(.enable("false"), .width(8)) multiplexer_1 (
    .in0(data_write), .in1({8{1'b0}}), .out(multiplexer_1_out), .sel(and_1_out));
  Decoder #(.enable("false"), .select(2)) decoder_1 (
    .out0(decoder_1_out0), .out1(decoder_1_out1), .out2(decoder_1_out2), .out3(decoder_1_out3),
    .sel(write_reg));
  and and_2 (and_2_out, write_enable, decoder_1_out0);
  and and_3 (and_3_out, write_enable, decoder_1_out1);
  and and_4 (and_4_out, write_enable, decoder_1_out2);
  and and_5 (and_5_out, write_enable, decoder_1_out3);
  Register Reg0 (.D(multiplexer_1_out), .en(and_2_out), .clk(clk), .Q(Reg0_q), .clr(reset));
  Register Reg1 (.D(multiplexer_1_out), .en(and_3_out), .clk(clk), .Q(Reg1_q), .clr(reset));
  Register Reg2 (.D(multiplexer_1_out), .en(and_4_out), .clk(clk), .Q(Reg2_q), .clr(reset));
  Register Reg3 (.D(multiplexer_1_out), .en(and_5_out), .clk(clk), .Q(Reg3_q), .clr(reset));
  Multiplexer #(.enable("false"), .select(2), .width(8)) multiplexer_2 (
    .in0(Reg0_q), .in1(Reg1_q), .in2(Reg2_q), .in3(Reg3_q), .out(data_read), .sel(read_reg));
endmodule

module alu (
  input  [7:0] A,
  input  [7:0] B,
  input  op,
  output [7:0] data_out
);

  wire [7:0] adder_1_out, demultiplexer_1_out0, demultiplexer_1_out1, demultiplexer_2_out0,
       demultiplexer_2_out1, subtractor_1_out;

  Demultiplexer #(.enable("false"), .width(8)) demultiplexer_1 (
    .out0(demultiplexer_1_out0), .out1(demultiplexer_1_out1), .in(A), .sel(op));
  Demultiplexer #(.enable("false"), .width(8)) demultiplexer_2 (
    .out0(demultiplexer_2_out0), .out1(demultiplexer_2_out1), .in(B), .sel(op));
  Adder adder_1 (.a(demultiplexer_1_out0), .b(demultiplexer_2_out0), .out(adder_1_out));  // open: cin, cout
  Subtractor subtractor_1 (
    .a(demultiplexer_1_out1), .b(demultiplexer_2_out1), .out(subtractor_1_out));  // open: bin, bout
  Multiplexer #(.enable("false"), .width(8)) multiplexer_1 (
    .in0(adder_1_out), .in1(subtractor_1_out), .out(data_out), .sel(op));
endmodule

module instr_decoder (
  input  [7:0] instr,
  output [1:0] imm,
  output [1:0] read_reg,
  output [1:0] write_reg,
  output write_en,
  output alu_op,
  output reg_clear
);

  wire decoder_1_out0;

  Decoder #(.enable("false"), .select(2)) decoder_1 (
    .out0(decoder_1_out0), .out2(alu_op), .out3(reg_clear), .sel(instr[7:6]));  // open: out1
  not not_1 (write_en, decoder_1_out0);

  assign imm = instr[1:0];
  assign read_reg = instr[3:2];
  assign write_reg = instr[5:4];
endmodule

module main (
  input  [7:0] Instruction
);

  wire Clk_out, instr_decoder_1_alu_op, instr_decoder_1_reg_clear, instr_decoder_1_write_en, Reset_out;
  wire [1:0] instr_decoder_1_imm, instr_decoder_1_read_reg, instr_decoder_1_write_reg;
  wire [7:0] alu_1_data_out, bit_extender_1_out, register_file_1_data_read;

  instr_decoder instr_decoder_1 (
    .instr(Instruction), .imm(instr_decoder_1_imm), .read_reg(instr_decoder_1_read_reg),
    .write_reg(instr_decoder_1_write_reg), .write_en(instr_decoder_1_write_en),
    .alu_op(instr_decoder_1_alu_op), .reg_clear(instr_decoder_1_reg_clear));
  Button Reset (.out(Reset_out));
  assign bit_extender_1_out = {{6{1'b0}}, instr_decoder_1_imm};  // Bit_Extender bit_extender_1
  Button Clk (.out(Clk_out));
  alu alu_1 (
    .A(register_file_1_data_read), .B(bit_extender_1_out), .op(instr_decoder_1_alu_op),
    .data_out(alu_1_data_out));
  register_file register_file_1 (
    .data_read(register_file_1_data_read), .clear(instr_decoder_1_reg_clear), .data_write(alu_1_data_out),
    .write_enable(instr_decoder_1_write_en), .write_reg(instr_decoder_1_write_reg), .clk(Clk_out),
    .reset(Reset_out), .read_reg(instr_decoder_1_read_reg));
endmodule
